// Logisim project main.circ as structural Verilog: 5 circuits, main circuit Magnitude-Comparator
// Is full?
module Magnitude_Comparator (
  input  in_1,
  input  in_2,
  input  in_3,
  input  in_4,
  input  in_5,
  input  in_6,
  input  in_7,
  input  in_8,
  output out_9
);

  wire xnor_1_out, xnor_2_out, xnor_3_out, xnor_4_out;

  xnor xnor_1 (xnor_1_out, in_1, in_2);
  xnor xnor_2 (xnor_2_out, in_3, in_4);
  xnor xnor_3 (xnor_3_out, in_5, in_6);
  xnor xnor_4 (xnor_4_out, in_7, in_8);
  and and_1 (out_9, xnor_1_out, xnor_2_out, xnor_3_out, xnor_4_out);
endmodule

// Counter
module Up_Down_Counter (
  input  Up_Down_prime,
  input  Reset,
  input  EN,
  output LSB,
  output out_5,
  output out_6,
  output MSB
);

  wire and_1_out, and_2_out, and_3_out, and_4_out, and_5_out, and_6_out, CLK_out, j_k_ff_1_qn, j_k_ff_2_qn,
       j_k_ff_3_qn, not_1_out, or_1_out, or_2_out, or_3_out;

  Clock CLK (.out(CLK_out));
  not not_1 (not_1_out, Up_Down_prime);
  J_K_Flip_Flop j_k_ff_1 (
    .J(1'b1), .clk(CLK_out), .K(1'b1), .Q(LSB), .Qn(j_k_ff_1_qn), .en(EN), .reset(Reset));  // open: preset
  and and_1 (and_1_out, Up_Down_prime, LSB);
  and and_2 (and_2_out, j_k_ff_1_qn, not_1_out, not_1_out);
  or or_1 (or_1_out, and_1_out, and_2_out);
  J_K_Flip_Flop j_k_ff_2 (
    .J(or_1_out), .clk(CLK_out), .K(or_1_out), .Q(out_5), .Qn(j_k_ff_2_qn), .en(EN), .reset(Reset));  // open: preset
  and and_3 (and_3_out, and_1_out, out_5);
  and and_4 (and_4_out, j_k_ff_2_qn, and_2_out);
  or or_2 (or_2_out, and_3_out, and_4_out);
  J_K_Flip_Flop j_k_ff_3 (
    .J(or_2_out), .clk(CLK_out), .K(or_2_out), .Q(out_6), .Qn(j_k_ff_3_qn), .en(EN), .reset(Reset));  // open: preset
  and and_5 (and_5_out, and_3_out, out_6);
  and and_6 (and_6_out, j_k_ff_3_qn, and_4_out);
  or or_3 (or_3_out, and_5_out, and_6_out);
  J_K_Flip_Flop j_k_ff_4 (
    .J(or_3_out), .clk(CLK_out), .K(or_3_out), .Q(MSB), .en(EN), .reset(Reset));  // open: Qn, preset
endmodule

module Main_Area (
  input  Main_Switch,
  input  _0_Enq_1_Deq,
  input  [1:0] ID,
  input  [1:0] Priority,
  output MSB,
  output out_6,
  output out_7,
  output LSB
);

  wire and_1_out, magnitude_comparator_1_out_9, multiplexer_1_out, not_1_out;
  wire [1:0] demultiplexer_1_out0;

  Demultiplexer demultiplexer_1 (
    .out0(demultiplexer_1_out0[0]), .out1(demultiplexer_1_out0[1]), .in(1'b1), .sel(_0_Enq_1_Deq),
    .en(Main_Switch));
  Multiplexer #(.select(2)) multiplexer_1 (
    .in0(1'b0), .in1(1'b1), .in2(1'b0), .in3(1'b0), .out(multiplexer_1_out), .sel(demultiplexer_1_out0));  // open: en
  not not_1 (not_1_out, magnitude_comparator_1_out_9);
  and and_1 (and_1_out, multiplexer_1_out, not_1_out);
  newinput newinput_1 (
    ._2b_Input(ID), ._2b_Priority(Priority), .EN(demultiplexer_1_out0[0]));  // open: out_4, out_5, out_6, LSB_A0, out_8, out_9, out_10, LSB_A1, out_12, out_13, out_14, LSB_A2, out_16, out_17, out_18, LSB_A3
  LED led_1 (.in(magnitude_comparator_1_out_9));
  Magnitude_Comparator magnitude_comparator_1 (
    .in_1(1'b1), .in_2(LSB), .in_3(1'b1), .in_4(out_7), .in_5(1'b1), .in_6(out_6), .in_7(1'b1), .in_8(MSB),
    .out_9(magnitude_comparator_1_out_9));
  Up_Down_Counter up_down_counter_1 (
    .Up_Down_prime(and_1_out), .LSB(LSB), .out_5(out_7), .out_6(out_6), .MSB(MSB));  // open: Reset, EN

  // Notes on the sheet:
  //   Use CTRL+T to run a clock pulse 
  //   NUMBER OF PATIENTS IN ROOM-BINARY OUTPUT
endmodule

module Shift_Register (
  input  MSB,
  input  in_2,
  input  in_3,
  input  LSB,
  input  EN,
  input  Reset,
  output MSB_2,
  output out_8,
  output out_9,
  output LSB_2
);

  wire CLK_out, d_ff_1_q, d_ff_2_q, d_ff_3_q, d_ff_4_q, d_ff_5_q, d_ff_6_q, d_ff_7_q, d_ff_8_q, d_ff_9_q,
       d_ff_10_q, d_ff_11_q, d_ff_12_q;

  Clock CLK (.out(CLK_out));
  D_Flip_Flop d_ff_1 (.clk(CLK_out), .D(MSB), .Q(d_ff_1_q), .en(EN), .reset(Reset));  // open: Qn, preset
  D_Flip_Flop d_ff_2 (.clk(CLK_out), .D(in_2), .Q(d_ff_2_q), .en(EN), .reset(Reset));  // open: Qn, preset
  D_Flip_Flop d_ff_3 (.clk(CLK_out), .D(in_3), .Q(d_ff_3_q), .en(EN), .reset(Reset));  // open: Qn, preset
  D_Flip_Flop d_ff_4 (.clk(CLK_out), .D(LSB), .Q(d_ff_4_q), .en(EN), .reset(Reset));  // open: Qn, preset
  D_Flip_Flop d_ff_5 (.clk(CLK_out), .D(d_ff_1_q), .Q(d_ff_5_q), .en(EN), .reset(Reset));  // open: Qn, preset
  D_Flip_Flop d_ff_6 (.clk(CLK_out), .D(d_ff_2_q), .Q(d_ff_6_q), .en(EN), .reset(Reset));  // open: Qn, preset
  D_Flip_Flop d_ff_7 (.clk(CLK_out), .D(d_ff_3_q), .Q(d_ff_7_q), .en(EN), .reset(Reset));  // open: Qn, preset
  D_Flip_Flop d_ff_8 (.clk(CLK_out), .D(d_ff_4_q), .Q(d_ff_8_q), .en(EN), .reset(Reset));  // open: Qn, preset
  D_Flip_Flop d_ff_9 (.clk(CLK_out), .D(d_ff_5_q), .Q(d_ff_9_q), .en(EN), .reset(Reset));  // open: Qn, preset
  D_Flip_Flop d_ff_10 (.clk(CLK_out), .D(d_ff_6_q), .Q(d_ff_10_q), .en(EN), .reset(Reset));  // open: Qn, preset
  D_Flip_Flop d_ff_11 (.clk(CLK_out), .D(d_ff_7_q), .Q(d_ff_11_q), .en(EN), .reset(Reset));  // open: Qn, preset
  D_Flip_Flop d_ff_12 (.clk(CLK_out), .D(d_ff_8_q), .Q(d_ff_12_q), .en(EN), .reset(Reset));  // open: Qn, preset
  D_Flip_Flop d_ff_13 (.clk(CLK_out), .D(d_ff_9_q), .Q(MSB_2), .en(EN), .reset(Reset));  // open: Qn, preset
  D_Flip_Flop d_ff_14 (.clk(CLK_out), .D(d_ff_10_q), .Q(out_8), .en(EN), .reset(Reset));  // open: Qn, preset
  D_Flip_Flop d_ff_15 (.clk(CLK_out), .D(d_ff_11_q), .Q(out_9), .en(EN), .reset(Reset));  // open: Qn, preset
  D_Flip_Flop d_ff_16 (.clk(CLK_out), .D(d_ff_12_q), .Q(LSB_2), .en(EN), .reset(Reset));  // open: Qn, preset
endmodule

module newinput (
  input  [1:0] _2b_Input,
  input  [1:0] _2b_Priority,
  input  EN,
  output out_4,
  output out_5,
  output out_6,
  output LSB_A0,
  output out_8,
  output out_9,
  output out_10,
  output LSB_A1,
  output out_12,
  output out_13,
  output out_14,
  output LSB_A2,
  output out_16,
  output out_17,
  output out_18,
  output LSB_A3
);

  wire demultiplexer_1_out0, demultiplexer_1_out1, demultiplexer_1_out2, demultiplexer_1_out3;

  Shift_Register shift_register_1 (
    .MSB(_2b_Input[1]), .in_2(_2b_Input[0]), .in_3(_2b_Priority[1]), .LSB(_2b_Priority[0]),
    .EN(demultiplexer_1_out0), .MSB_2(out_4), .out_8(out_5), .out_9(out_6), .LSB_2(LSB_A0));  // open: Reset
  Demultiplexer #(.select(2), .enable("false")) demultiplexer_1 (
    .out0(demultiplexer_1_out0), .out1(demultiplexer_1_out1), .out2(demultiplexer_1_out2),
    .out3(demultiplexer_1_out3), .in(EN), .sel(_2b_Priority));
  Shift_Register shift_register_2 (
    .MSB(_2b_Input[1]), .in_2(_2b_Input[0]), .in_3(_2b_Priority[1]), .LSB(_2b_Priority[0]),
    .EN(demultiplexer_1_out1), .MSB_2(out_8), .out_8(out_9), .out_9(out_10), .LSB_2(LSB_A1));  // open: Reset
  Shift_Register shift_register_3 (
    .MSB(_2b_Input[1]), .in_2(_2b_Input[0]), .in_3(_2b_Priority[1]), .LSB(_2b_Priority[0]),
    .EN(demultiplexer_1_out2), .MSB_2(out_12), .out_8(out_13), .out_9(out_14), .LSB_2(LSB_A2));  // open: Reset
  Shift_Register shift_register_4 (
    .MSB(_2b_Input[1]), .in_2(_2b_Input[0]), .in_3(_2b_Priority[1]), .LSB(_2b_Priority[0]),
    .EN(demultiplexer_1_out3), .MSB_2(out_16), .out_8(out_17), .out_9(out_18), .LSB_2(LSB_A3));  // open: Reset
endmodule
